# Fritzing sketch dht11 fritzing (saved by Fritzing 0.8.7b)
breadboards: 1

parts:
  Eleman2 = Arduino Uno (Rev3)
  Eleman3 = LCD1602-I2C
  DHT1 = DHT11 Humitidy and Temperature Sensor

nets:
  N1: Eleman2.A4/SDA, Eleman3.SDA
  N2: Eleman2.A5/SCL, Eleman3.SCL
  N3: Eleman2.D2, DHT1.DATA
  5V: Eleman2.5V, Eleman3.VCC, DHT1.VDD
  GND: Eleman2.GND, Eleman3.GND, DHT1.GND

notes:
  Aeduino UNO
  DHT11 Sıcaklık ve nem sensörü
  16x2 LCD Ekran
  CCC

custom parts:
  LCD1602-I2C: A standard character display, usually with 2x16 characters. Comes in many colors with LCM1602 IIC attached.
  DHT11 Humitidy and Temperature Sensor: DHT11 Humidity and Temperature Sensor
