# Fritzing sketch gelgelbalonfritzing (saved by Fritzing 0.8.7b)
breadboards: 1

parts:
  Arduino_UNO = Arduino Uno (Rev3)
  Servo = Basic Servo
  PIR_ensör = PIR sensor

nets:
  N1: Arduino_UNO.D8, PIR_ensör.SIG
  5V: Arduino_UNO.5V, Servo.vcc, PIR_ensör.VDD
  GND: Arduino_UNO.GND, Servo.gnd, PIR_ensör.GND

notes:
  EL SALLAYAN BALON
