# Fritzing sketch lcd ile gelgelbalonfritzing (saved by Fritzing 0.8.7b)
breadboards: 1

parts:
  Arduino_UNO = Arduino Uno (Rev3)
  Servo = Basic Servo
  LCD_Ekran = LCD1602-I2C
  PIR_Sensör = PIR sensor

nets:
  N1: Arduino_UNO.A0, LCD_Ekran.SDA
  N2: Arduino_UNO.A1, LCD_Ekran.SCL
  N3: Arduino_UNO.D8, PIR_Sensör.SIG
  VCC: Arduino_UNO.5V, Servo.vcc, LCD_Ekran.VCC, PIR_Sensör.VDD
  GND: Arduino_UNO.GND, Servo.gnd, LCD_Ekran.GND, PIR_Sensör.GND

notes:
  EL SALLAYAN BALON LCD'Lİ

custom parts:
  LCD1602-I2C: A standard character display, usually with 2x16 characters. Comes in many colors with LCM1602 IIC attached.
