# Fritzing sketch Hırsız alarm sistemi buton led ve lcd kontrol fritzing (saved by Fritzing 0.8.7b)
breadboards: 1

parts:
  BUZZER = Piezo Speaker
  TUŞ1 = Momentary Switch [package=ksa_sealed_tac_switch]
  LED = LED - 5mm [color="Red (633nm)" package="5 mm [THT]"]
  TUŞ2 = Momentary Switch [package=ksa_sealed_tac_switch]
  R1 = Resistor [tolerance=±5% resistance=220 package=THT]
  R2 = Resistor [tolerance=±5% resistance=220 package=THT]
  Eleman1 = Arduino Uno (Rev3)
  LED2 = LED - 5mm [color="Red (633nm)" package="5 mm [THT]"]
  R3 = Resistor [tolerance=±5% resistance=220 package=THT]
  R4 = Resistor [tolerance=±5% resistance=220 package=THT]
  Eleman2 = LCD1602-I2C
  PIR1 = PIR sensor

nets:
  GND: BUZZER.pin1, LED.cathode, R1.Pin_1, R2.Pin_1, Eleman1.GND, LED2.cathode, Eleman2.GND, PIR1.GND
  5V: TUŞ1.1, TUŞ2.1, Eleman1.5V, Eleman2.VCC, PIR1.VDD
  N1: TUŞ1.3, R1.Pin_0
  N2: TUŞ1.4, Eleman1.D12/MISO
  N3: LED.anode, R3.Pin_0
  N4: TUŞ2.3, R2.Pin_0
  N5: TUŞ2.4, Eleman1.D11_PWM/MOSI
  N6: Eleman1.A0, Eleman2.SDA
  N7: Eleman1.A1, Eleman2.SCL
  N8: Eleman1.D2, PIR1.SIG
  N9: Eleman1.D3_PWM, R3.Pin_1
  N10: Eleman1.D4, R4.Pin_1
  N11: LED2.anode, R4.Pin_0

notes:
  HAREKET SENSÖRÜ İLE ALARM SİSTEMİ LCD EKRANLI

custom parts:
  LCD1602-I2C: A standard character display, usually with 2x16 characters. Comes in many colors with LCM1602 IIC attached.
