# Fritzing sketch Hırsız alarm sistemi led kontrol fritzing (saved by Fritzing 0.8.7b)
breadboards: 1

parts:
  BUZZER = Piezo Speaker
  TUŞ1 = Momentary Switch [package=ksa_sealed_tac_switch]
  LED = LED - 5mm [color="Red (633nm)" package="5 mm [THT]"]
  TUŞ = Momentary Switch [package=ksa_sealed_tac_switch]
  R1 = Resistor [tolerance=±5% resistance=220 package=THT]
  R2 = Resistor [tolerance=±5% resistance=220 package=THT]
  Arduino_UNO = Arduino Uno (Rev3)
  LED2 = LED - 5mm [color="Red (633nm)" package="5 mm [THT]"]
  R3 = Resistor [tolerance=±5% resistance=220 package=THT]
  Direnç = Resistor [tolerance=±5% resistance=220 package=THT]
  PIR_sensör = PIR sensor

nets:
  GND: BUZZER.pin1, LED.cathode, R1.Pin_1, R2.Pin_1, Arduino_UNO.GND, LED2.cathode, PIR_sensör.GND
  5V: TUŞ1.1, TUŞ.1, Arduino_UNO.5V, PIR_sensör.VDD
  N1: TUŞ1.3, R1.Pin_0
  N2: TUŞ1.4, Arduino_UNO.D12/MISO
  N3: LED.anode, R3.Pin_0
  N4: TUŞ.3, R2.Pin_0
  N5: TUŞ.4, Arduino_UNO.D11_PWM/MOSI
  N6: Arduino_UNO.D2, PIR_sensör.SIG
  N7: Arduino_UNO.D3_PWM, R3.Pin_1
  N8: Arduino_UNO.D4, Direnç.Pin_1
  N9: LED2.anode, Direnç.Pin_0

notes:
  HAREKET SENSÖRÜ İLE ALARM SİSTEMİ
