# Fritzing sketch Gelişmiş park sensörü devre şeması (saved by Fritzing 0.8.7b)
breadboards: 1

parts:
  Eleman1 = SRF05 Ultrasonic Rangefinder
  Eleman2 = Arduino Uno (Rev3)
  J1 = Piezo Speaker
  LED1 = LED - 5mm [color="Red (633nm)" package="5 mm [THT]"]
  R1 = Resistor [tolerance=±5% resistance=220 package=THT]
  LED2 = LED - 5mm [color="Red (633nm)" package="5 mm [THT]"]
  LED3 = LED - 5mm [color="Red (633nm)" package="5 mm [THT]"]
  R2 = Resistor [tolerance=±5% resistance=220 package=THT]
  R3 = Resistor [tolerance=±5% resistance=220 package=THT]

nets:
  VCC: Eleman1.VCC, Eleman2.5V
  N1: Eleman1.Trig, Eleman2.D9_PWM
  N2: Eleman1.Echo, Eleman2.D8
  GND: Eleman1.GND, Eleman2.GND, J1.pin1, LED1.cathode, LED2.cathode, LED3.cathode
  N3: Eleman2.D3_PWM, R2.Pin_1
  N4: Eleman2.D5_PWM, R1.Pin_1
  N5: Eleman2.D6_PWM, R3.Pin_1
  N6: Eleman2.3V3, J1.pin2
  N7: LED1.anode, R1.Pin_0
  N8: LED2.anode, R2.Pin_0
  N9: LED3.anode, R3.Pin_0

notes:
  Aeduino UNO
  HC-SR04 Ultrasonik Mesaf e Sensörü
  16x2 LCD Ekran
  LEDLİ PARK SENSÖRÜ
  Buzzer
  LED
