# Fritzing sketch Park Sensoru fritzing (saved by Fritzing 0.8.7b)
breadboards: 1

parts:
  Eleman1 = SRF05 Ultrasonic Rangefinder
  Eleman2 = Arduino Uno (Rev3)
  J1 = Piezo Speaker

nets:
  VCC: Eleman1.VCC, Eleman2.5V
  N1: Eleman1.Trig, Eleman2.D9_PWM
  N2: Eleman1.Echo, Eleman2.D8
  GND: Eleman1.GND, Eleman2.GND, J1.pin1
  N3: Eleman2.D12/MISO, J1.pin2

notes:
  Aeduino UNO
  HC-SR04 Ultrasonik Mesaf e Sensörü
  16x2 LCD Ekran
  PARK SENSÖRÜ
  Buzzer
