# Fritzing sketch uzaklık hesaplama fritzing (saved by Fritzing 0.8.7b)
breadboards: 1

parts:
  Eleman1 = SRF05 Ultrasonic Rangefinder
  Eleman2 = Arduino Uno (Rev3)
  Eleman3 = LCD1602-I2C

nets:
  VCC: Eleman1.VCC, Eleman2.5V, Eleman3.VCC
  N1: Eleman1.Trig, Eleman2.D9_PWM
  N2: Eleman1.Echo, Eleman2.D8
  GND: Eleman1.GND, Eleman2.GND, Eleman3.GND
  N3: Eleman2.A4/SDA, Eleman3.SDA
  N4: Eleman2.A5/SCL, Eleman3.SCL

notes:
  Aeduino UNO
  HC-SR04 Ultrasonik Mesaf e Sensörü
  16x2 LCD Ekran
  MESAFE ÖLÇER

custom parts:
  LCD1602-I2C: A standard character display, usually with 2x16 characters. Comes in many colors with LCM1602 IIC attached.
