# Fritzing sketch kapı kilit sistemi fritzing (saved by Fritzing 0.8.7b)
breadboards: 1

parts:
  J1 = female pin header, 8 pins [form="♀ (female)"]  # not connected
  Keypad4x1 = Keypad Membran 4x4
  Eleman1 = Arduino Uno (Rev3)
  J2 = Basic Servo
  LED1 = LED - 5mm [color="Red (633nm)" package="5 mm [THT]"]
  LED2 = LED - 5mm [color="Red (633nm)" package="5 mm [THT]"]
  R3 = Resistor [tolerance=±5% resistance=220 package=THT]
  R4 = Resistor [tolerance=±5% resistance=220 package=THT]

nets:
  N1: Keypad4x1.Pin1, Eleman1.D13/SCK
  N2: Keypad4x1.Pin2, Eleman1.D12/MISO
  N3: Keypad4x1.Pin3, Eleman1.D11_PWM/MOSI
  N4: Keypad4x1.Pin4, Eleman1.D10_PWM/SS
  N5: Keypad4x1.Pin5, Eleman1.D9_PWM
  N6: Keypad4x1.Pin6, Eleman1.D8
  N7: Keypad4x1.Pin7, Keypad4x1.Pin8, Eleman1.D6_PWM, Eleman1.D7
  N8: Eleman1.D2, R3.Pin_1
  N9: Eleman1.D3_PWM, J2.pulse
  N10: Eleman1.D4, R4.Pin_1
  N11: Eleman1.GND, LED1.cathode, LED2.cathode
  N12: LED1.anode, R3.Pin_0
  N13: LED2.anode, R4.Pin_0

notes:
  KAPI KİLİT SİSTEMİ

custom parts:
  Keypad Membran 4x4: Membrane Keypad 4x4 Matrix
