# Fritzing sketch keypad kullanımı fritzing (saved by Fritzing 0.8.7b)

parts:
  J1 = female pin header, 8 pins [form="♀ (female)"]  # not connected
  Keypad4x1 = Keypad Membran 4x4
  Eleman1 = Arduino Uno (Rev3)

nets:
  N1: Keypad4x1.Pin1, Eleman1.D13/SCK
  N2: Keypad4x1.Pin2, Eleman1.D12/MISO
  N3: Keypad4x1.Pin3, Eleman1.D11_PWM/MOSI
  N4: Keypad4x1.Pin4, Eleman1.D10_PWM/SS
  N5: Keypad4x1.Pin5, Eleman1.D9_PWM
  N6: Keypad4x1.Pin6, Eleman1.D8
  N7: Keypad4x1.Pin7, Keypad4x1.Pin8, Eleman1.D6_PWM, Eleman1.D7

notes:
  KAPI KİLİT SİSTEMİ

custom parts:
  Keypad Membran 4x4: Membrane Keypad 4x4 Matrix
