# Fritzing sketch LDR Kullanımı fritzing (saved by Fritzing 0.8.7b)
breadboards: 1

parts:
  LDR = Photocell (LDR) [package=THT]
  R2 = Resistor [tolerance=±5% resistance=220 package=THT]
  Direnç = Resistor [tolerance=±5% resistance=220 package=THT]
  LED1 = LED - 5mm [color="Red (633nm)" package="5 mm [THT]"]
  Arduino_UNO = Arduino Uno (Rev3)

nets:
  N1: LDR.pin_1, Direnç.Pin_0, Arduino_UNO.A0
  N2: R2.Pin_0, LED1.anode
  N3: R2.Pin_1, Arduino_UNO.D3_PWM
  N4: Direnç.Pin_1, LED1.cathode

notes:
  KARANLIKTA YANAN LED
