# Fritzing sketch gaz sensorufritzing (saved by Fritzing 0.8.7b)
breadboards: 1

parts:
  gaz_sensörü = GAS_SENSOR [package=mq-3]
  J1 = Piezo Speaker
  arduino_uno = Arduino Uno (Rev3)

nets:
  N1: gaz_sensörü.B1, arduino_uno.A0
  N2: J1.pin1, arduino_uno.GND
  N3: J1.pin2, arduino_uno.D9_PWM

notes:
  GAZ SENSÖRÜ
